// Logisim project XNORwTransistors.circ as structural Verilog: 1 circuit, main circuit main
module main (
  input  A,
  input  B,
  output A_XNOR_B
);

  wire transistor_2_out;

  Transistor #(.\type ("n")) transistor_1 (.in(A), .out(A_XNOR_B), .gate(B));
  Transistor transistor_2 (.in(1'b1), .out(transistor_2_out), .gate(A));
  Transistor transistor_3 (.in(transistor_2_out), .out(A_XNOR_B), .gate(B));
  Transistor #(.\type ("n")) transistor_4 (.in(B), .out(A_XNOR_B), .gate(A));
endmodule
