// Logisim project absval8.circ as structural Verilog: 1 circuit, main circuit main
module main (
  input  d7,
  input  d6,
  input  d5,
  input  d4,
  input  d3,
  input  d2,
  input  d1,
  input  d0,
  output n7,
  output n6,
  output n5,
  output n4,
  output n3,
  output n2,
  output n1,
  output n0
);

  wire and_1_out, and_2_out, and_3_out, and_4_out, and_5_out, and_6_out, not_1_out, not_2_out, not_3_out,
       not_4_out, not_5_out, not_6_out, not_7_out, not_8_out, xor_1_out, xor_2_out, xor_3_out, xor_4_out,
       xor_5_out, xor_6_out, xor_7_out;

  not not_1 (not_1_out, d7);
  xor xor_1 (xor_1_out, not_1_out, and_1_out);
  Multiplexer #(.enable("false")) multiplexer_1 (.in0(d7), .in1(xor_1_out), .out(n7), .sel(d7));
  and and_1 (and_1_out, not_2_out, and_2_out);
  not not_2 (not_2_out, d6);
  and and_2 (and_2_out, not_3_out, and_3_out);
  xor xor_2 (xor_2_out, not_2_out, and_2_out);
  Multiplexer #(.enable("false")) multiplexer_2 (.in0(d6), .in1(xor_2_out), .out(n6), .sel(d7));
  not not_3 (not_3_out, d5);
  xor xor_3 (xor_3_out, not_3_out, and_3_out);
  Multiplexer #(.enable("false")) multiplexer_3 (.in0(d5), .in1(xor_3_out), .out(n5), .sel(d7));
  and and_3 (and_3_out, not_4_out, and_4_out);
  not not_4 (not_4_out, d4);
  xor xor_4 (xor_4_out, not_4_out, and_4_out);
  Multiplexer #(.enable("false")) multiplexer_4 (.in0(d4), .in1(xor_4_out), .out(n4), .sel(d7));
  and and_4 (and_4_out, not_5_out, and_5_out);
  not not_5 (not_5_out, d3);
  xor xor_5 (xor_5_out, not_5_out, and_5_out);
  Multiplexer #(.enable("false")) multiplexer_5 (.in0(d3), .in1(xor_5_out), .out(n3), .sel(d7));
  and and_5 (and_5_out, not_6_out, and_6_out);
  not not_6 (not_6_out, d2);
  xor xor_6 (xor_6_out, not_6_out, and_6_out);
  Multiplexer #(.enable("false")) multiplexer_6 (.in0(d2), .in1(xor_6_out), .out(n2), .sel(d7));
  and and_6 (and_6_out, not_7_out, not_8_out);
  not not_7 (not_7_out, d1);
  Multiplexer #(.enable("false")) multiplexer_7 (.in0(d1), .in1(xor_7_out), .out(n1), .sel(d7));
  xor xor_7 (xor_7_out, not_7_out, not_8_out);
  not not_8 (not_8_out, d0);

  assign n0 = d0;
endmodule
