// Logisim project lowOne.circ as structural Verilog
module main (
  input  b0,
  input  b1,
  input  b2,
  input  b3,
  output error,
  output w0,
  output w1
);

  wire and_1_out, and_2_out, and_3_out, and_4_out, not_1_out, not_2_out, not_3_out, not_4_out, not_5_out,
       not_6_out, not_7_out, not_8_out, not_9_out, not_10_out, not_11_out;

  not not_1 (not_1_out, b3);
  not not_2 (not_2_out, b2);
  not not_3 (not_3_out, b1);
  not not_4 (not_4_out, b0);
  and and_1 (and_1_out, b1, not_5_out);
  not not_5 (not_5_out, b0);
  and and_2 (and_2_out, b3, not_6_out, not_7_out);
  not not_6 (not_6_out, b2);
  not not_7 (not_7_out, b0);
  and and_3 (and_3_out, b2, not_8_out, not_9_out);
  not not_8 (not_8_out, b1);
  not not_9 (not_9_out, b0);
  not not_10 (not_10_out, b1);
  and and_4 (and_4_out, b3, not_10_out, not_11_out);
  not not_11 (not_11_out, b0);
  and and_5 (error, not_1_out, not_2_out, not_3_out, not_4_out);
  or or_1 (w0, and_1_out, and_2_out);
  or or_2 (w1, and_3_out, and_4_out);
endmodule
